// Logisim project EXP 10.circ as structural Verilog: 1 circuit, main circuit main
module main (
  input  in_1,
  input  in_2,
  input  in_3,
  output out_4,
  output out_5
);

  wire AND_2_out, AND_3_out, AND_out, XOR_out;

  xor XOR (XOR_out, in_1, in_2);
  buf AND (AND_out, in_1);  // AND_Gate
  and AND_2 (AND_2_out, in_2, in_3);
  and AND_3 (AND_3_out, in_3, in_1);
  xor XOR_2 (out_4, XOR_out, in_3);
  or OR (out_5, AND_out, AND_2_out, AND_3_out);
endmodule
