// Logisim project EXP 11.circ as structural Verilog: 1 circuit, main circuit main
module main (
  input  in_1,
  input  in_2,
  output out_3,
  output out_4
);

  wire NAND_2_out, NAND_3_out, NAND_out;

  nand NAND (NAND_out, in_1, in_2);
  nand NAND_2 (NAND_2_out, in_1, NAND_out);
  nand NAND_3 (NAND_3_out, NAND_out, in_2);
  nand NAND_4 (out_3, NAND_2_out, NAND_3_out);
  nand NAND_5 (out_4, NAND_out, NAND_out);
endmodule
