// Logisim project EXP 9.circ as structural Verilog: 1 circuit, main circuit main
module main (
  input  A,
  input  B,
  output S,
  output out_4
);

  xor XOR (S, A, B);
  and AND (out_4, A, B);
endmodule
